// Logisim project BancoRegistros.circ as structural Verilog: 1 circuit, main circuit BancoRegistros
module BancoRegistros (
  input  CLR,
  input  [31:0] di,
  input  [2:0] a1,
  input  CLK,
  input  [2:0] ad,
  input  [2:0] a2,
  input  we,
  output [31:0] do1,
  output [31:0] do2
);

  wire demultiplexer_1_out1, demultiplexer_1_out2, demultiplexer_1_out3, demultiplexer_1_out4,
       demultiplexer_1_out5, demultiplexer_1_out6, demultiplexer_1_out7;
  wire [31:0] R0_q, R1_q, R2_q, R3_q, R4_q, R5_q, R6_q, R7_q;

  Demultiplexer #(.select(3)) demultiplexer_1 (
    .out1(demultiplexer_1_out1), .out2(demultiplexer_1_out2), .out3(demultiplexer_1_out3),
    .out4(demultiplexer_1_out4), .out5(demultiplexer_1_out5), .out6(demultiplexer_1_out6),
    .out7(demultiplexer_1_out7), .in(CLK), .sel(ad), .en(we));  // open: out0
  Register #(.width(32)) R0 (.Q(R0_q));  // open: D, en, clk, clr
  Register #(.width(32)) R1 (.D(di), .Q(R1_q), .clk(demultiplexer_1_out1), .clr(CLR));  // open: en
  Register #(.width(32)) R2 (.D(di), .Q(R2_q), .clk(demultiplexer_1_out2), .clr(CLR));  // open: en
  Register #(.width(32)) R3 (.D(di), .Q(R3_q), .clk(demultiplexer_1_out3), .clr(CLR));  // open: en
  Register #(.width(32)) R4 (.D(di), .Q(R4_q), .clk(demultiplexer_1_out4), .clr(CLR));  // open: en
  Register #(.width(32)) R5 (.D(di), .Q(R5_q), .clk(demultiplexer_1_out5), .clr(CLR));  // open: en
  Register #(.width(32)) R6 (.D(di), .Q(R6_q), .clk(demultiplexer_1_out6), .clr(CLR));  // open: en
  Register #(.width(32)) R7 (.D(di), .Q(R7_q), .clk(demultiplexer_1_out7), .clr(CLR));  // open: en
  Multiplexer #(.select(3), .width(32)) multiplexer_1 (
    .in0(R0_q), .in1(R1_q), .in2(R2_q), .in3(R3_q), .in4(R4_q), .in5(R5_q), .in6(R6_q), .in7(R7_q),
    .out(do1), .sel(a1));  // open: en
  Multiplexer #(.select(3), .width(32)) multiplexer_2 (
    .in0(R0_q), .in1(R1_q), .in2(R2_q), .in3(R3_q), .in4(R4_q), .in5(R5_q), .in6(R6_q), .in7(R7_q),
    .out(do2), .sel(a2));  // open: en

  // Notes on the sheet:
  //   Banco De Registros
  //   Designed by: Eng. Oscar Hurtado (TxOs) 
  //   Under License Creative Commons CC BY-SA
  //   https://creativecommons.org/share-your-work/cclicenses/
  //   BANCO DE REGISTROS
  //   Nota: El registro cero R0 siempre retorna el valor de 'cero'
endmodule
